# Fritzing sketch kos-v2.1 (saved by Fritzing 0.9.9b)
circuit board: 13.1938cm x 7.15711cm
breadboards: 1

parts:
  S1 = Kailh Choc Switch [package=THT]
  S2 = Kailh Choc Switch [package=THT]
  S3 = Kailh Choc Switch [package=THT]
  S4 = Kailh Choc Switch [package=THT]
  S5 = Kailh Choc Switch [package=THT]
  S6 = Kailh Choc Switch [package=THT]
  S8 = Kailh Choc Switch [package=THT]
  S9 = Kailh Choc Switch [package=THT]
  S10 = Kailh Choc Switch [package=THT]
  S11 = Kailh Choc Switch [package=THT]
  S12 = Kailh Choc Switch [package=THT]
  S13 = Kailh Choc Switch [package=THT]
  S14 = Kailh Choc Switch [package=THT]
  S15 = Kailh Choc Switch [package=THT]
  D1 = Rectifier Diode [package="Melf DO-213 AA [SMD]"]
  D2 = Rectifier Diode [package="Melf DO-213 AA [SMD]"]
  D3 = Rectifier Diode [package="Melf DO-213 AA [SMD]"]
  D4 = Rectifier Diode [package="Melf DO-213 AA [SMD]"]
  D5 = Rectifier Diode [package="Melf DO-213 AA [SMD]"]
  D6 = Rectifier Diode [package="Melf DO-213 AA [SMD]"]
  D7 = Rectifier Diode [package="Melf DO-213 AA [SMD]"]
  D8 = Rectifier Diode [package="Melf DO-213 AA [SMD]"]
  D9 = Rectifier Diode [package="Melf DO-213 AA [SMD]"]
  D10 = Rectifier Diode [package="Melf DO-213 AA [SMD]"]
  D11 = Rectifier Diode [package="Melf DO-213 AA [SMD]"]
  D12 = Rectifier Diode [package="Melf DO-213 AA [SMD]"]
  D19 = Rectifier Diode [package="Melf DO-213 AA [SMD]"]
  D20 = Rectifier Diode [package="Melf DO-213 AA [SMD]"]
  D25 = Rectifier Diode [package="Melf DO-213 AA [SMD]"]
  S27 = Kailh Choc Switch [package=THT]
  S29 = Kailh Choc Switch [package=THT]
  S30 = Kailh Choc Switch [package=THT]
  S17 = Kailh Choc Switch [package=THT]
  S19 = Kailh Choc Switch [package=THT]
  S22 = Kailh Choc Switch [package=THT]
  S26 = Kailh Choc Switch [package=THT]
  S18 = Kailh Choc Switch [package=THT]
  S24 = Kailh Choc Switch [package=THT]
  S28 = Kailh Choc Switch [package=THT]
  S25 = Kailh Choc Switch [package=THT]
  S16 = Kailh Choc Switch [package=THT]
  S23 = Kailh Choc Switch [package=THT]
  S20 = Kailh Choc Switch [package=THT]
  S21 = Kailh Choc Switch [package=THT]
  D16 = Rectifier Diode [package="Melf DO-213 AA [SMD]"]
  D27 = Rectifier Diode [package="Melf DO-213 AA [SMD]"]
  D30 = Rectifier Diode [package="Melf DO-213 AA [SMD]"]
  D18 = Rectifier Diode [package="Melf DO-213 AA [SMD]"]
  D17 = Rectifier Diode [package="Melf DO-213 AA [SMD]"]
  D26 = Rectifier Diode [package="Melf DO-213 AA [SMD]"]
  D23 = Rectifier Diode [package="Melf DO-213 AA [SMD]"]
  D21 = Rectifier Diode [package="Melf DO-213 AA [SMD]"]
  D28 = Rectifier Diode [package="Melf DO-213 AA [SMD]"]
  D29 = Rectifier Diode [package="Melf DO-213 AA [SMD]"]
  D22 = Rectifier Diode [package="Melf DO-213 AA [SMD]"]
  D24 = Rectifier Diode [package="Melf DO-213 AA [SMD]"]
  Pad14 = Pad [width=5 height=2 connect=center]
  Pad15 = Pad [width=5 height=2 connect=center]
  Pad16 = Pad [width=5 height=2 connect=center]
  Pad17 = Pad [width=5 height=2 connect=center]
  Pad18 = Pad [width=5 height=2 connect=center]
  Pad19 = Pad [width=5 height=2 connect=center]
  Pad20 = Pad [width=5 height=2 connect=center]
  Pad21 = Pad [width=5 height=2 connect=center]
  Pad22 = Pad [width=5 height=2 connect=center]
  Pad23 = Pad [width=5 height=2 connect=center]
  Pad24 = Pad [width=5 height=2 connect=center]
  Pad1 = Pad [width=5 height=2 connect=center]
  Pad2 = Pad [width=5 height=2 connect=center]
  Pad3 = Pad [width=5 height=2 connect=center]
  Pad4 = Pad [width=5 height=2 connect=center]
  Pad5 = Pad [width=5 height=2 connect=center]
  Pad6 = Pad [width=5 height=2 connect=center]
  Pad7 = Pad [width=5 height=2 connect=center]
  Pad8 = Pad [width=5 height=2 connect=center]
  Pad9 = Pad [width=5 height=2 connect=center]
  Pad10 = Pad [width=5 height=2 connect=center]
  Pad11 = Pad [width=5 height=2 connect=center]
  D13 = Rectifier Diode [package="Melf DO-213 AA [SMD]"]
  D14 = Rectifier Diode [package="Melf DO-213 AA [SMD]"]
  D15 = Rectifier Diode [package="Melf DO-213 AA [SMD]"]
  J2 = female pin header, 2 pins [form="♀ (female)"]
  J3 = female pin header, 2 pins [form="♀ (female)"]
  J4 = female pin header, 2 pins [form="♀ (female)"]
  J5 = female pin header, 2 pins [form="♀ (female)"]
  J6 = female pin header, 2 pins [form="♀ (female)"]
  J7 = female pin header, 2 pins [form="♀ (female)"]
  J8 = female pin header, 2 pins [form="♀ (female)"]
  J9 = female pin header, 2 pins [form="♀ (female)"]
  J10 = female pin header, 2 pins [form="♀ (female)"]
  J11 = female pin header, 2 pins [form="♀ (female)"]
  J12 = female pin header, 2 pins [form="♀ (female)"]
  J13 = female pin header, 2 pins [form="♀ (female)"]
  J14 = female pin header, 2 pins [form="♀ (female)"]
  J15 = female pin header, 2 pins [form="♀ (female)"]
  J16 = female pin header, 2 pins [form="♀ (female)"]
  J18 = female pin header, 20 pins [form="♀ (female)"]
  Pad25 = Pad [width=5 height=2 connect=center]
  Pad26 = Pad [width=5 height=2 connect=center]
  Pad27 = Pad [width=5 height=2 connect=center]
  Pad28 = Pad [width=5 height=2 connect=center]
  Pad29 = Pad [width=5 height=2 connect=center]
  Pad31 = Pad [width=5 height=2 connect=center]
  Pad32 = Pad [width=5 height=2 connect=center]
  Pad33 = Pad [width=5 height=2 connect=center]
  Pad34 = Pad [width=5 height=2 connect=center]
  Pad36 = Pad [width=5 height=2 connect=center]
  Pad37 = Pad [width=5 height=2 connect=center]
  Pad38 = Pad [width=5 height=2 connect=center]
  Pad39 = Pad [width=5 height=2 connect=center]
  Pad40 = Pad [width=5 height=2 connect=center]
  Pad41 = Pad [width=5 height=2 connect=center]
  Pad42 = Pad [width=5 height=2 connect=center]
  Pad43 = Pad [width=5 height=2 connect=center]
  Pad44 = Pad [width=5 height=2 connect=center]
  S7 = Kailh Choc Switch [package=THT]

nets:
  N1: S1.leg0, S13.leg0, S27.leg0, S29.leg0, S23.leg0, Pad14.pad, Pad8.pad, J18.pin9, S7.leg0
  N2: S1.leg1, D1.anode, S27.leg1, D16.anode, J2.pin2
  N3: S2.leg0, S8.leg0, S14.leg0, S30.leg0, S17.leg0, S20.leg0, Pad17.pad, Pad9.pad, J18.pin10
  N4: S2.leg1, D2.anode, S17.leg1, D27.anode, J3.pin2
  N5: S3.leg0, S9.leg0, S15.leg0, S19.leg0, S28.leg0, S21.leg0, Pad15.pad, Pad11.pad, J18.pin12
  N6: S3.leg1, D3.anode, S28.leg1, D30.anode, J4.pin2
  N7: S4.leg0, S10.leg0, S22.leg0, S24.leg0, J18.pin14, Pad25.pad, Pad37.pad
  N8: S4.leg1, D4.anode, S24.leg1, D18.anode, J5.pin2
  N9: S5.leg0, S11.leg0, S26.leg0, S25.leg0, J18.pin15, Pad27.pad, Pad38.pad
  N10: S5.leg1, D5.anode, S25.leg1, D28.anode, J6.pin2
  N11: S6.leg0, S12.leg0, S18.leg0, S16.leg0, J18.pin16, Pad32.pad, Pad39.pad
  N12: S6.leg1, D6.anode, S16.leg1, D22.anode, J7.pin2
  N13: S8.leg1, D8.anode, S30.leg1, D26.anode, J12.pin2
  N14: S9.leg1, D9.anode, S19.leg1, D23.anode, J11.pin2
  N15: S10.leg1, D10.anode, S22.leg1, D21.anode, J10.pin2
  N16: S11.leg1, D11.anode, S26.leg1, D29.anode, J9.pin2
  N17: S12.leg1, D12.anode, S18.leg1, D24.anode, J8.pin2
  N18: S13.leg1, D19.anode, S23.leg1, D13.anode, J16.pin2
  N19: S14.leg1, D20.anode, S20.leg1, D14.anode, J15.pin2
  N20: S15.leg1, D25.anode, S21.leg1, D15.anode, J14.pin2
  N21: D1.cathode, D2.cathode, D3.cathode, D4.cathode, D5.cathode, D6.cathode, D16.cathode, D27.cathode, D30.cathode, D18.cathode, D28.cathode, D22.cathode, Pad24.pad, Pad6.pad, J2.pin1, J3.pin1, J4.pin1, J5.pin1, J6.pin1, J7.pin1, J18.pin7
  N22: D7.cathode, D8.cathode, D9.cathode, D10.cathode, D11.cathode, D12.cathode, D17.cathode, D26.cathode, D23.cathode, D21.cathode, D29.cathode, D24.cathode, J8.pin1, J9.pin1, J10.pin1, J11.pin1, J12.pin1, J13.pin1, J18.pin17, Pad29.pad, Pad40.pad
  N23: D7.anode, S29.leg1, D17.anode, J13.pin2, S7.leg1
  N24: D19.cathode, D20.cathode, D25.cathode, D13.cathode, D14.cathode, D15.cathode, J14.pin1, J15.pin1, J16.pin1, J18.pin20, Pad28.pad, Pad43.pad
  N25: Pad16.pad, Pad5.pad, J18.pin6
  N26: Pad18.pad, Pad4.pad, J18.pin5
  N27: Pad19.pad, Pad2.pad, J18.pin3
  N28: Pad20.pad, J18.pin13, Pad36.pad
  N29: Pad21.pad, Pad3.pad, J18.pin4
  N30: Pad22.pad, Pad7.pad, J18.pin8
  N31: Pad23.pad, Pad10.pad, J18.pin11
  N32: Pad1.pad, J18.pin2, Pad33.pad
  N33: J18.pin1, Pad34.pad, Pad44.pad
  N34: J18.pin18, Pad26.pad, Pad41.pad
  N35: J18.pin19, Pad31.pad, Pad42.pad

notes:
  Kos v2.1

custom parts:
  Kailh Choc Switch: A generic pushbutton.
